# Fritzing sketch breadboard_audio_circuit (saved by Fritzing 0.9.6b)
breadboards: 1

parts:
  U2 = 555 Timer [package="DIP8 [THT]"]
  C1 = Capacitor [package=cap-pth-small2]
  C3 = Capacitor [package=cap-pth-small2]
  R1 = Resistor [tolerance=±5% power=0.25 resistance=10k package=THT]
  R2 = Resistor [tolerance=±5% power=0.25 resistance=4.7k package=THT]
  D1 = Diode [package=diode-hv]
  C4 = Electrolytic Capacitor [capacitance=1µF voltage=35V package="100 mil [THT, electrolytic]"]
  SP1 = SPEAKER [package=pcb_mount_speaker]

nets:
  N1: U2.Ground, SP1.+
  N2: U2.Trigger, U2.Threshold, C1.2, R2.Pin_1
  N3: U2.Output, C4.-
  N4: U2.Control_Voltage, C3.2
  N5: U2.Discharge, R1.Pin_1, R2.Pin_0, D1.C
  N6: U2.Vcc_Supply_Voltage, C1.1, C3.1, R1.Pin_0
  N7: C4.+, SP1.-

notes:
  1uF
  10nF
  100uF
  8 Ohm 0.5W
