# Fritzing sketch breadboard_cd40110BE (saved by Fritzing 0.9.6b)
breadboards: 3

parts:
  S4 = Pushbutton [package="[THT]"]
  S5 = Pushbutton [package="[THT]"]
  7_Segment1 = 7 Segment Display
  R1 = Resistor [tolerance=±5% power=0.25 resistance=1k package=THT]
  IC1 = CD40110BE [package="DIP16 [THT]"]
  R2 = Resistor [tolerance=±5% power=0.25 resistance=1k package=THT]
  R3 = Resistor [tolerance=±5% power=0.25 resistance=470 package=THT]

nets:
  N1: S4.Pin_1, S4.Pin_2, S5.Pin_1, S5.Pin_2
  N2: S4.Pin_3, S4.Pin_4, R1.Pin_1, IC1.In_7
  N3: S5.Pin_3, S5.Pin_4, IC1.COM_-_Common, R2.Pin_0
  N4: 7_Segment1.Segment_E, IC1.Out_5
  N5: 7_Segment1.Segment_D, IC1.Out_4
  N6: 7_Segment1.common_cathode, R3.Pin_0
  N7: 7_Segment1.Segment_C, IC1.Out_3
  N8: 7_Segment1.Segment_B, IC1.Out_2
  N9: 7_Segment1.Segment_A, IC1.In_1
  N10: 7_Segment1.Segment_F, IC1.In_3
  N11: 7_Segment1.Segment_G, IC1.In_2
  N12: R1.Pin_0, IC1.In_5, IC1.In_6, IC1.0V
  N13: IC1.Out_7, IC1.Out_6, R2.Pin_1

notes:
  Up
  Down

custom parts:
  CD40110BE: ULN2003A 7-way Darlington Transistor Driver
