# Fritzing sketch breadboard_set_and_count (saved by Fritzing 0.9.6b)
breadboards: 3

parts:
  S3 = Pushbutton [package="[THT]"]
  S4 = Pushbutton [package="[THT]"]
  S5 = Pushbutton [package="[THT]"]
  C1 = Capacitor [package=cap-pth-small2]
  R1 = Resistor [tolerance=±5% resistance=1k power=0.25 package=THT]
  U1 = CD4013BE [part_number=CD4013BE package="DIP (Dual Inline) [THT]"]
  Part1 = CD4013BE [part_number=CD4013BE package="DIP (Dual Inline) [THT]"]  # not connected
  U1_1 = CD4013BE [part_number=CD4013BE package="DIP (Dual Inline) [THT]"]  # not connected
  U1_2 = CD4013BE [part_number=CD4013BE package="DIP (Dual Inline) [THT]"]  # not connected
  U1_3 = CD4013BE [part_number=CD4013BE package="DIP (Dual Inline) [THT]"]  # not connected
  U1_4 = CD4013BE [part_number=CD4013BE package="DIP (Dual Inline) [THT]"]  # not connected
  R2 = Resistor [tolerance=±5% resistance=1k power=0.25 package=THT]
  C2 = Capacitor [package=cap-pth-small2]
  U2 = 555 Timer [package="DIP8 [THT]"]
  R3 = Resistor [tolerance=±5% resistance=10k power=0.25 package=THT]
  R4 = Resistor [tolerance=±5% resistance=10k power=0.25 package=THT]
  U3 = 555 Timer [package="DIP8 [THT]"]
  R5 = Resistor [tolerance=±5% resistance=10k power=0.25 package=THT]
  R6 = Resistor [tolerance=±5% resistance=10k power=0.25 package=THT]
  C3 = Capacitor [package=cap-pth-small2]
  C4 = Capacitor [package=cap-pth-small2]
  IC1 = CD40110BE [package="DIP16 [THT]"]
  7_Segment2 = 7 Segment Display
  R7 = Resistor [tolerance=±5% resistance=470 power=0.25 package=THT]
  R8 = Resistor [tolerance=±5% resistance=10k power=0.25 package=THT]
  R9 = Resistor [tolerance=±5% resistance=10k power=0.25 package=THT]

nets:
  N1: S3.Pin_1, S3.Pin_2, S4.Pin_1, S4.Pin_2, S5.Pin_1, S5.Pin_2, C1.2, C2.1
  N2: S3.Pin_3, S3.Pin_4, C1.1, R1.Pin_0, U1.connector2
  N3: S4.Pin_3, S4.Pin_4, IC1.COM_-_Common, R9.Pin_1
  N4: S5.Pin_3, S5.Pin_4, U3.Output, IC1.In_7, R8.Pin_1
  N5: R1.Pin_1, U1.connector5, U1.connector6, R2.Pin_1, U2.Ground, U3.Ground, IC1.In_4, IC1.In_6, IC1.0V
  N6: U1.connector0, U2.Trigger, R3.Pin_1
  N7: U1.connector1, U1.connector4, U2.Reset, R4.Pin_1
  N8: U1.connector3, R2.Pin_0, C2.2
  N9: U1.connector7, U1.connector9, U1.connector10, U1.connector11, U1.connector12, U2.Control_Voltage, U2.Threshold, U2.Discharge, C3.1, IC1.Out_7, IC1.Out_6
  N10: U1.connector13, U2.Vcc_Supply_Voltage, IC1.Out_1
  N11: U2.Output, U3.Vcc_Supply_Voltage, R5.Pin_0
  N12: R3.Pin_0, R4.Pin_0, U3.Reset
  N13: U3.Trigger, U3.Threshold, R6.Pin_0, C4.2
  N14: U3.Control_Voltage, C3.2
  N15: U3.Discharge, R5.Pin_1, R6.Pin_1
  N16: C4.1, R7.Pin_0
  N17: IC1.In_1, 7_Segment2.Segment_A
  N18: IC1.In_2, 7_Segment2.Segment_G
  N19: IC1.In_3, 7_Segment2.Segment_F
  N20: IC1.Out_5, 7_Segment2.Segment_E
  N21: IC1.Out_4, 7_Segment2.Segment_D
  N22: IC1.Out_3, 7_Segment2.Segment_C
  N23: IC1.Out_2, 7_Segment2.Segment_B
  N24: 7_Segment2.common_cathode, R7.Pin_1
  N25: R8.Pin_0, R9.Pin_0

notes:
  Start/Stop
  Up
  Down

custom parts:
  CD4013BE: 4071 4 x 2 Input OR Gate with sub-parts
  CD4013BE: 4071 4 x 2 Input OR Gate with sub-parts
  CD4013BE: 4071 4 x 2 Input OR Gate with sub-parts
  CD4013BE: 4071 4 x 2 Input OR Gate with sub-parts
  CD4013BE: 4071 4 x 2 Input OR Gate with sub-parts
  CD4013BE: 4071 4 x 2 Input OR Gate with sub-parts
  CD40110BE: ULN2003A 7-way Darlington Transistor Driver
