# Fritzing sketch breadboard_start_stop (saved by Fritzing 0.9.6b)
breadboards: 3

parts:
  S3 = Pushbutton [package="[THT]"]
  S4 = Pushbutton [package="[THT]"]
  S5 = Pushbutton [package="[THT]"]
  C1 = Capacitor [package=cap-pth-small2]
  R1 = Resistor [tolerance=±5% resistance=1k package=THT]
  U1 = CD4013BE [part_number=CD4013BE package="DIP (Dual Inline) [THT]"]
  part = CD4013BE [part_number=CD4013BE package="DIP (Dual Inline) [THT]"]  # not connected
  U1_1 = CD4013BE [part_number=CD4013BE package="DIP (Dual Inline) [THT]"]  # not connected
  U1_2 = CD4013BE [part_number=CD4013BE package="DIP (Dual Inline) [THT]"]  # not connected
  U1_3 = CD4013BE [part_number=CD4013BE package="DIP (Dual Inline) [THT]"]  # not connected
  U1_4 = CD4013BE [part_number=CD4013BE package="DIP (Dual Inline) [THT]"]  # not connected
  R2 = Resistor [tolerance=±5% resistance=1k power=0.25 package=THT]
  C2 = Capacitor [package=cap-pth-small2]
  U2 = 555 Timer [package="DIP8 [THT]"]
  R3 = Resistor [tolerance=±5% resistance=10k power=0.25 package=THT]
  R4 = Resistor [tolerance=±5% resistance=10k power=0.25 package=THT]
  LED1 = LED - 5mm [color="Red (633nm)" current=0.030 package="5 mm [THT]"]
  R5 = Resistor [tolerance=±5% resistance=1k power=0.25 package=THT]

nets:
  N1: S3.Pin_1, S3.Pin_2, C1.2, C2.1
  N2: S3.Pin_3, S3.Pin_4, C1.1, R1.Pin_0, U1.connector2
  N3: S4.Pin_1, S4.Pin_2
  N4: S4.Pin_3, S4.Pin_4
  N5: S5.Pin_1, S5.Pin_2
  N6: S5.Pin_3, S5.Pin_4
  N7: R1.Pin_1, U1.connector5, U1.connector6, R2.Pin_1, U2.Ground
  N8: U1.connector0, U2.Trigger, R3.Pin_1
  N9: U1.connector1, U1.connector4, U2.Reset, R4.Pin_1
  N10: U1.connector3, R2.Pin_0, C2.2
  N11: U1.connector7, U1.connector9, U1.connector10, U1.connector11, U1.connector12, U2.Control_Voltage, U2.Threshold, U2.Discharge
  N12: U1.connector13, U2.Vcc_Supply_Voltage
  N13: U2.Output, LED1.cathode
  N14: R3.Pin_0, R4.Pin_0
  N15: LED1.anode, R5.Pin_0

notes:
  Start/Stop
  Up
  Down

custom parts:
  CD4013BE: 4071 4 x 2 Input OR Gate with sub-parts
  CD4013BE: 4071 4 x 2 Input OR Gate with sub-parts
  CD4013BE: 4071 4 x 2 Input OR Gate with sub-parts
  CD4013BE: 4071 4 x 2 Input OR Gate with sub-parts
  CD4013BE: 4071 4 x 2 Input OR Gate with sub-parts
  CD4013BE: 4071 4 x 2 Input OR Gate with sub-parts
